# Fritzing sketch gluno (saved by Fritzing 0.8.7b)
breadboards: 1

parts:
  Part1 = Arduino BT
  R1 = Resistor [tolerance=±5% resistance=10k package=THT]
  R2 = Resistor [tolerance=±5% resistance=10k package=THT]
  Q1 = NPN-Transistor [package="TO92 [THT]"]
  R3 = Resistor [tolerance=±5% resistance=300 package=THT]

nets:
  N1: Part1.SS/PWM_D10, R1.Pin_1
  N2: Part1.GND, R2.Pin_1, Q1.E
  N3: Part1.5V, R3.Pin_0
  N4: R1.Pin_0, Q1.B
  N5: R2.Pin_0, Q1.C, R3.Pin_1

notes:
  300Ω
  10kΩ
  8050 npn
  E-B-C
  血糖仪
  RX－发给血糖仪的信号－反向TTL
  TX－发给MCU的信号－TTL
  GND
